# Fritzing sketch ArduinoUNO (saved by Fritzing 0.9.3b)
circuit board: 7.72811cm x 4.23631cm
breadboards: 1

parts:
  VCC1 = Battery
  U2 = Voltage Regulator - 5V [package="TO220 [THT]"]
  XTAL1 = Crystal [frequency="16 Mhz" package=THT]
  C1 = Ceramic Capacitor [capacitance=22µF package="100 mil [THT, multilayer]"]
  S1 = Pushbutton [package="[THT]"]
  LED1 = LED - 5mm [color="Red (633nm)" package="5 mm [THT]"]
  R3 = Resistor [tolerance=±5% resistance=10 package=THT]
  C2 = Ceramic Capacitor [capacitance=100nF package="100 mil [THT, multilayer]"]
  U1 = atmega328 [package=dip]
  R2 = Resistor [tolerance=±5% resistance=220 package=THT]

nets:
  GND: VCC1.-, U2.GND, C1.1, R3.Pin_1, C2.0, U1.GND, R2.Pin_1
  N1: VCC1.+, U2.input_voltage
  N2: U2.output_voltage, U1.VCC, U1.AVCC
  N3: XTAL1.pin_0, C1.0, U1.XLAT2
  N4: XTAL1.pin_1, C2.1, U1.XLAT1
  N5: S1.Pin_1, S1.Pin_2, U1.RESET
  N6: S1.Pin_4, R3.Pin_0
  N7: LED1.cathode, R2.Pin_0
  N8: LED1.anode, U1.D13
